# Fritzing sketch WeatherLogger (saved by Fritzing 0.9.2b)
breadboards: 1

parts:
  Breakout1 = BMP280 [package=Breakout]
  Raspberry_Pi1 = Raspberry Pi B+
  LED1 = LEDs [package=led10mm]
  R1 = Resistor [tolerance=±5% resistance=220 package="0805 [SMD]"]

nets:
  VIN: Breakout1.VIN, Raspberry_Pi1.5V
  GND: Breakout1.GND, Raspberry_Pi1.GND
  N1: Breakout1.SCK, Raspberry_Pi1.GPIO3
  N2: Breakout1.SDI, Raspberry_Pi1.GPIO2
  N3: Raspberry_Pi1.3V3, R1.Pin_1
  N4: Raspberry_Pi1.GIPO12, LED1.A
  N5: LED1.C, R1.Pin_0

custom parts:
  BMP280: Barometric Pressure and Temperature Sensor
  Raspberry Pi B+: The awesome Raspberry Pi ARM Board with 40 pin gipo. Ready for special designed Raspberry Pi B+ Hat (Hardware attached (on) top)
